// Logisim project Microprocessor.circ as structural Verilog
module CPU (
  output out_1
);

  wire ALU_cout, clock_1_out, CU_add, CU_and, CU_clr_ac, CU_clr_ar, CU_clr_pc, CU_clr_sc_2, CU_com, CU_d_e,
       CU_dr_2, CU_en_e, CU_en_i, CU_inpr, CU_inr_ac, CU_inr_ar, CU_inr_dr, CU_inr_pc, CU_j_fgi, CU_j_fgo,
       CU_j_ien, CU_j_r, CU_j_s, CU_k_ien, CU_k_r, CU_ld_ac, CU_ld_ar, CU_ld_dr, CU_ld_ir, CU_ld_outr,
       CU_ld_pc, CU_ld_tr, CU_mem_read, CU_mem_wr, CU_shl, CU_shr, CU_x1, CU_x2, CU_x3, CU_x4, CU_x5, CU_x6,
       CU_x7, E_q, FGI_q, FGO_q, I_q, IEN_q, or_1_out, or_2_out, R_q, S_q, START_out;
  wire [2:0] Encoder_out;
  wire [7:0] INPR_out;
  wire [11:0] AR_out, multiplexer_1_out, PC_out;
  wire [15:0] AC_out, ALU_out, DR_out, IR_out, ram_1_data, TR_out;
  wire [15:12] multiplexer_1_out_2;

  Clock clock_1 (.out(clock_1_out));
  Button START (.out(START_out));
  Control_Unit CU (
    .DR(or_1_out), .AC(or_2_out), .AC_15(AC_out[15]), .FGO(FGO_q), .FGI(FGI_q), .IEN(IEN_q), .E(E_q),
    .I(I_q), .R(R_q), .IR_12(IR_out[12]), .IR_13(IR_out[13]), .IR_14(IR_out[14]), .CLR_SC(CU_clr_sc_2),
    .LOAD_SC(1'b0), .INR_SC(S_q), .CLK(clock_1_out), .B0(IR_out[0]), .B1(IR_out[1]), .B2(IR_out[2]),
    .B3(IR_out[3]), .B4(IR_out[4]), .B5(IR_out[5]), .B6(IR_out[6]), .B7(IR_out[7]), .B8(IR_out[8]),
    .B9(IR_out[9]), .B10(IR_out[10]), .B11(IR_out[11]), .COUT(ALU_cout), .A_0(AC_out[0]), .En_I(CU_en_i),
    .LD_TR(CU_ld_tr), .LD_AR(CU_ld_ar), .CLR_AR(CU_clr_ar), .INR_AR(CU_inr_ar), .CLR_PC(CU_clr_pc),
    .LD_PC(CU_ld_pc), .LD_IR(CU_ld_ir), .K_R(CU_k_r), .INR_PC(CU_inr_pc), .INR_DR(CU_inr_dr),
    .LD_DR(CU_ld_dr), .LD_OUTR(CU_ld_outr), .J_FGO(CU_j_fgo), .CLR_SC_2(CU_clr_sc_2), .LD_AC(CU_ld_ac),
    .J_FGI(CU_j_fgi), .INR_AC(CU_inr_ac), .CLR_AC(CU_clr_ac), .MEM_WR(CU_mem_wr), .MEM_READ(CU_mem_read),
    .En_E(CU_en_e), .D_E(CU_d_e), .J_R(CU_j_r), .J_IEN(CU_j_ien), .K_IEN(CU_k_ien), .J_S(CU_j_s), .X1(CU_x1),
    .X2(CU_x2), .X3(CU_x3), .X4(CU_x4), .X5(CU_x5), .X6(CU_x6), .X7(CU_x7), .AND(CU_and), .ADD(CU_add),
    .DR_2(CU_dr_2), .INPR(CU_inpr), .COM(CU_com), .SHR(CU_shr), .SHL(CU_shl), .t0(out_1));
  D_Flip_Flop I (.clk(clock_1_out), .D(IR_out[15]), .Q(I_q), .en(CU_en_i));  // open: Qn, preset, reset
  J_K_Flip_Flop R (.J(CU_j_r), .clk(clock_1_out), .K(CU_k_r), .Q(R_q));  // open: Qn, preset, en, reset
  J_K_Flip_Flop IEN (.J(CU_j_ien), .clk(clock_1_out), .K(CU_k_ien), .Q(IEN_q));  // open: Qn, preset, en, reset
  J_K_Flip_Flop FGI (.J(1'b0), .clk(clock_1_out), .K(CU_j_fgi), .Q(FGI_q));  // open: Qn, preset, en, reset
  J_K_Flip_Flop FGO (.J(1'b0), .clk(clock_1_out), .K(CU_j_fgo), .Q(FGO_q));  // open: Qn, preset, en, reset
  J_K_Flip_Flop S (.J(1'b0), .clk(clock_1_out), .K(CU_j_s), .Q(S_q), .preset(START_out));  // open: Qn, en, reset
  Encoder Encoder (
    .x1(CU_x1), .x2(CU_x2), .x3(CU_x3), .x4(CU_x4), .x5(CU_x5), .x6(CU_x6), .x7(CU_x7), .out(Encoder_out));
  D_Flip_Flop E (.clk(clock_1_out), .D(CU_d_e), .Q(E_q), .en(CU_en_e));  // open: Qn, preset, reset
  _16_bit_Als_Unit ALU (
    .AC(AC_out), .DR(DR_out), .AND(CU_and), .ADD(CU_add), .DR_2(CU_dr_2), .INPR(CU_inpr), .INPR_IN(INPR_out),
    .COM(CU_com), .SHR(CU_shr), .SHL(CU_shl), .AC_i_1_2(E_q), .AC_i_1(E_q), .Cin(1'b0), .OUT(ALU_out),
    .Cout(ALU_cout));
  or or_1 (or_1_out, DR_out[15], DR_out[14], DR_out[13], DR_out[12], DR_out[11], DR_out[10], DR_out[9], DR_out[8], DR_out[7], DR_out[6], DR_out[5], DR_out[4], DR_out[3], DR_out[2], DR_out[1], DR_out[0]);
  RAM #(.addrWidth(12), .dataWidth(16), .bus("separate")) ram_1 (
    .addr(AR_out), .din({multiplexer_1_out_2, multiplexer_1_out}), .data(ram_1_data), .str(CU_mem_wr),
    .clk(clock_1_out), .ld(CU_mem_read));  // open: sel, clr
  Combined_12_bit_Register AR (
    .CLR(CU_clr_ar), .LOAD(CU_ld_ar), .INR(CU_inr_ar), .IN(multiplexer_1_out), .CLK(clock_1_out),
    .OUT(AR_out), .CLR_AS(START_out));  // open: STAGE
  Combined_12_bit_Register PC (
    .CLR(CU_clr_pc), .LOAD(CU_ld_pc), .INR(CU_inr_pc), .IN(multiplexer_1_out), .CLK(clock_1_out),
    .OUT(PC_out), .CLR_AS(START_out));  // open: STAGE
  Combined_16_bit_Register DR (
    .CLR(1'b0), .LOAD(CU_ld_dr), .INR(CU_inr_dr), .IN({multiplexer_1_out_2, multiplexer_1_out}),
    .CLK(clock_1_out), .OUT(DR_out));  // open: STAGE
  Combined_16_bit_Register AC (
    .CLR(CU_clr_ac), .LOAD(CU_ld_ac), .INR(CU_inr_ac), .IN(ALU_out), .CLK(clock_1_out), .OUT(AC_out));  // open: STAGE
  Combined_16_bit_Register IR (
    .CLR(1'b0), .LOAD(CU_ld_ir), .INR(1'b0), .IN({multiplexer_1_out_2, multiplexer_1_out}),
    .CLK(clock_1_out), .OUT(IR_out));  // open: STAGE
  Combined_16_bit_Register TR (
    .CLR(1'b0), .LOAD(CU_ld_tr), .INR(1'b0), .IN({multiplexer_1_out_2, multiplexer_1_out}),
    .CLK(clock_1_out), .OUT(TR_out));  // open: STAGE
  _8_Bit_Register INPR (.CLK(clock_1_out), .OUT(INPR_out));  // open: CLR, LOAD, INR, IN, STAGE
  _8_Bit_Register OUTPR (
    .LOAD(CU_ld_outr), .IN(multiplexer_1_out[7:0]), .CLK(clock_1_out));  // open: CLR, INR, OUT, STAGE
  Multiplexer #(.select(3), .width(16)) multiplexer_1 (
    .in1({4'b0000, AR_out}), .in2({4'b0000, PC_out}), .in3(DR_out), .in4(AC_out), .in5(IR_out), .in6(TR_out),
    .in7(ram_1_data), .out({multiplexer_1_out_2, multiplexer_1_out}), .sel(Encoder_out));  // open: in0, en
  or or_2 (or_2_out, AC_out[15], AC_out[14], AC_out[13], AC_out[12], AC_out[11], AC_out[10], AC_out[9], AC_out[8], AC_out[7], AC_out[6], AC_out[5], AC_out[4], AC_out[3], AC_out[2], AC_out[1], AC_out[0]);
endmodule

module Control_Unit (
  input  DR,
  input  AC,
  input  AC_15,
  input  FGO,
  input  FGI,
  input  IEN,
  input  E,
  input  I,
  input  R,
  input  IR_12,
  input  IR_13,
  input  IR_14,
  input  CLR_SC,
  input  LOAD_SC,
  input  INR_SC,
  input  CLK,
  input  B0,
  input  B1,
  input  B2,
  input  B3,
  input  B4,
  input  B5,
  input  B6,
  input  B7,
  input  B8,
  input  B9,
  input  B10,
  input  B11,
  input  COUT,
  input  A_0,
  output En_I,
  output LD_TR,
  output LD_AR,
  output CLR_AR,
  output INR_AR,
  output CLR_PC,
  output LD_PC,
  output LD_IR,
  output K_R,
  output INR_PC,
  output INR_DR,
  output LD_DR,
  output t0,
  output LD_OUTR,
  output J_FGO,
  output CLR_SC_2,
  output LD_AC,
  output AND,
  output ADD,
  output DR_2,
  output INPR,
  output COM,
  output SHR,
  output SHL,
  output J_FGI,
  output INR_AC,
  output CLR_AC,
  output MEM_WR,
  output MEM_READ,
  output En_E,
  output D_E,
  output J_R,
  output J_IEN,
  output K_IEN,
  output J_S,
  output X1,
  output X2,
  output X3,
  output X4,
  output X5,
  output X6,
  output X7
);

  wire and_2_out, and_3_out, and_4_out, and_5_out, and_6_out, control_sequencer_1_d0, control_sequencer_1_d1,
       control_sequencer_1_d2, control_sequencer_1_d3, control_sequencer_1_d4, control_sequencer_1_d5,
       control_sequencer_1_d6, control_sequencer_1_d7, control_sequencer_1_t1, control_sequencer_1_t2,
       control_sequencer_1_t3, control_sequencer_1_t4, control_sequencer_1_t5, control_sequencer_1_t6,
       D3T4_out, D4T4_out, D5T5_out, D6T6_out, D6T6DR_prime_out, D7_prime_IT3_2_out, D7_prime_IT3_out,
       not_1_out, not_2_out, not_3_out, not_4_out, not_5_out, not_6_out, not_7_out, not_8_out, not_9_out,
       not_10_out, not_11_out, or_1_out, or_2_out, p_out, pB6_out, pB8FGO_out, pB9FGI_out, r_out,
       R_prime_T0_out, rB1E_prime_out, rB2AC_prime_out, rB3A15_out, rB4A15_prime_out, rB8_out, rB10_out;

  not not_1 (not_1_out, DR);
  not not_2 (not_2_out, AC);
  not not_3 (not_3_out, AC_15);
  not not_4 (not_4_out, E);
  not not_5 (not_5_out, I);
  not not_6 (not_6_out, R);
  Control_sequencer control_sequencer_1 (
    .CLR_SC(CLR_SC), .LOAD_SC(LOAD_SC), .INR_SC(INR_SC), .CLK(CLK), .D0(control_sequencer_1_d0),
    .D1(control_sequencer_1_d1), .D2(control_sequencer_1_d2), .D3(control_sequencer_1_d3),
    .D4(control_sequencer_1_d4), .D5(control_sequencer_1_d5), .D6(control_sequencer_1_d6),
    .D7(control_sequencer_1_d7), .T0(t0), .T1(control_sequencer_1_t1), .T2(control_sequencer_1_t2),
    .T3(control_sequencer_1_t3), .T4(control_sequencer_1_t4), .T5(control_sequencer_1_t5),
    .T6(control_sequencer_1_t6), .IR_14(IR_14), .IR_13(IR_13), .IR_12(IR_12));  // open: STAGE
  or or_1 (or_1_out, FGO, FGI);
  and u_r (r_out, control_sequencer_1_d7, not_5_out, control_sequencer_1_t3);
  and p (p_out, control_sequencer_1_d7, I, control_sequencer_1_t3);
  not not_7 (not_7_out, control_sequencer_1_d7);
  not not_8 (not_8_out, control_sequencer_1_t1);
  not not_9 (not_9_out, control_sequencer_1_t2);
  not not_10 (not_10_out, control_sequencer_1_d7);
  not not_11 (not_11_out, t0);
  and R_prime_T0 (R_prime_T0_out, not_6_out, t0);
  and R_prime_T2 (En_I, not_6_out, control_sequencer_1_t2);
  and D7_prime_IT3 (D7_prime_IT3_out, not_7_out, I, control_sequencer_1_t3);
  and RT0 (CLR_AR, t0, R);
  and D5T4 (INR_AR, control_sequencer_1_d5, control_sequencer_1_t4);
  and RT1 (CLR_PC, R, control_sequencer_1_t1);
  and D4T4 (D4T4_out, control_sequencer_1_d4, control_sequencer_1_t4);
  and D5T5 (D5T5_out, control_sequencer_1_d5, control_sequencer_1_t5);
  and R_prime_T1 (LD_IR, not_6_out, control_sequencer_1_t1);
  and RT2 (K_R, R, control_sequencer_1_t2);
  and D6T6DR_prime (D6T6DR_prime_out, control_sequencer_1_d6, control_sequencer_1_t6, not_1_out);
  and rB4A15_prime (rB4A15_prime_out, r_out, B4, not_3_out);
  and rB3A15 (rB3A15_out, r_out, B3, AC_15);
  and rB2AC_prime (rB2AC_prime_out, r_out, B2, not_2_out);
  and rB1E_prime (rB1E_prime_out, r_out, B1, not_4_out);
  and pB9FGI (pB9FGI_out, p_out, B9, FGI);
  and pB8FGO (pB8FGO_out, p_out, B8, FGO);
  and D6T5 (INR_DR, control_sequencer_1_d6, control_sequencer_1_t5);
  or or_2 (or_2_out, control_sequencer_1_d0, control_sequencer_1_d1, control_sequencer_1_d2, control_sequencer_1_d6);
  // AND_Gate D6T5_2 has open pins: in0=control_sequencer_1_d6, in1=control_sequencer_1_t5, out=open
  and PB10 (J_FGO, p_out, B10);
  and D0T5 (AND, control_sequencer_1_d0, control_sequencer_1_t5);
  and D2T5 (DR_2, control_sequencer_1_d2, control_sequencer_1_t5);
  and D1T5 (ADD, control_sequencer_1_d1, control_sequencer_1_t5);
  and D3T4 (D3T4_out, control_sequencer_1_d3, control_sequencer_1_t4);
  and D6T6 (D6T6_out, control_sequencer_1_d6, control_sequencer_1_t6);
  and rB9 (COM, r_out, B9);
  and rB7 (SHR, r_out, B7);
  and rB6 (SHL, r_out, B6);
  and pB11 (INPR, p_out, B11);
  and rB5 (INR_AC, r_out, B5);
  and rB11 (CLR_AC, r_out, B11);
  and D7_prime_IT3_2 (D7_prime_IT3_2_out, not_10_out, I, control_sequencer_1_t3);
  and rB10 (rB10_out, r_out, B10);
  and rB8 (rB8_out, r_out, B8);
  and pB7 (J_IEN, p_out, B7);
  and pB6 (pB6_out, p_out, B6);
  and rB0 (J_S, B0, r_out);
  and and_1 (LD_DR, or_2_out, control_sequencer_1_t4);
  or or_3 (LD_AR, R_prime_T0_out, En_I, D7_prime_IT3_out);
  or or_4 (LD_PC, D4T4_out, D5T5_out);
  or or_5 (MEM_WR, CLR_PC, D3T4_out, INR_AR, D6T6_out);
  or or_6 (MEM_READ, LD_DR, LD_IR, D7_prime_IT3_2_out);
  or or_7 (En_E, ADD, SHR, SHL, rB10_out, rB8_out);
  and and_2 (and_2_out, COUT, ADD);
  and and_3 (and_3_out, A_0, SHR);
  and and_4 (and_4_out, AC_15, SHL);
  and and_5 (and_5_out, 1'b0, rB10_out);
  and and_6 (and_6_out, not_4_out, rB8_out);
  and and_7 (J_R, not_11_out, not_8_out, not_9_out, IEN, or_1_out);
  or or_8 (K_IEN, pB6_out, K_R);
  or or_9 (INR_PC, LD_IR, K_R, D6T6DR_prime_out, rB4A15_prime_out, rB3A15_out, rB2AC_prime_out, rB1E_prime_out, pB9FGI_out, pB8FGO_out);
  or or_10 (CLR_SC_2, K_R, AND, DR_2, ADD, D3T4_out, D4T4_out, D5T5_out, D6T6_out, p_out, r_out);
  or or_11 (LD_AC, AND, ADD, DR_2, COM, SHR, SHL, INPR);
  or or_12 (D_E, and_2_out, and_3_out, and_4_out, and_5_out, and_6_out);
  or or_13 (X2, R_prime_T0_out, CLR_AR, INR_AR);
  or or_14 (X3, DR_2, D6T6_out);
  or or_15 (X4, J_FGO, D3T4_out);

  assign J_FGI = INPR;
  assign LD_OUTR = J_FGO;
  assign LD_TR = CLR_AR;
  assign X1 = LD_PC;
  assign X5 = En_I;
  assign X6 = CLR_PC;
  assign X7 = MEM_READ;
endmodule

module Control_sequencer (
  input  IR_14,
  input  IR_13,
  input  IR_12,
  input  CLR_SC,
  input  LOAD_SC,
  input  INR_SC,
  input  CLK,
  output D0,
  output D1,
  output D2,
  output D3,
  output D4,
  output D5,
  output D6,
  output D7,
  output T0,
  output T1,
  output T2,
  output T3,
  output T4,
  output T5,
  output T6,
  output STAGE
);

  wire [3:0] n4_bit_rgister_1_a0;

  Decoder #(.select(3)) decoder_1 (
    .out0(D0), .out1(D1), .out2(D2), .out3(D3), .out4(D4), .out5(D5), .out6(D6), .out7(D7),
    .sel({IR_14, IR_13, IR_12}));  // open: en
  _4_Bit_Rgister u_4_bit_rgister_1 (
    .CLR(CLR_SC), .LOAD(LOAD_SC), .INR(INR_SC), .I0(1'b0), .I1(1'b0), .I2(1'b0), .I3(1'b0), .CLK(CLK),
    .A0(n4_bit_rgister_1_a0[0]), .A1(n4_bit_rgister_1_a0[1]), .A2(n4_bit_rgister_1_a0[2]),
    .A3(n4_bit_rgister_1_a0[3]), .STAGE(STAGE));
  Decoder #(.select(4)) decoder_2 (
    .out0(T0), .out1(T1), .out2(T2), .out3(T3), .out4(T4), .out5(T5), .out6(T6), .sel(n4_bit_rgister_1_a0));  // open: out7, out8, out9, out10, out11, out12, out13, out14, out15, en
endmodule

module _16_bit_Als_Unit (
  input  [15:0] AC,
  input  [15:0] DR,
  input  AC_i_1,
  input  Cin,
  input  AND,
  input  ADD,
  input  DR_2,
  input  INPR,
  input  [7:0] INPR_IN,
  input  COM,
  input  SHR,
  input  SHL,
  input  AC_i_1_2,
  output [15:0] OUT,
  output Cout
);

  wire n1_bit_als_unit_1_c_i_1, n1_bit_als_unit_2_c_i_1, n1_bit_als_unit_3_c_i_1, n1_bit_als_unit_4_c_i_1,
       n1_bit_als_unit_5_c_i_1, n1_bit_als_unit_6_c_i_1, n1_bit_als_unit_7_c_i_1, n1_bit_als_unit_8_c_i_1,
       n1_bit_als_unit_9_c_i_1, n1_bit_als_unit_10_c_i_1, n1_bit_als_unit_11_c_i_1, n1_bit_als_unit_12_c_i_1,
       n1_bit_als_unit_13_c_i_1, n1_bit_als_unit_14_c_i_1, n1_bit_als_unit_15_c_i_1;

  _1_bit_ALS_unit u_1_bit_als_unit_1 (
    .AC_i(AC[0]), .DR_i(DR[0]), .AND(AND), .ADD(ADD), .DR(DR_2), .INPR(INPR), .INPR_i(INPR_IN[0]), .COM(COM),
    .SHR(SHR), .AC_i_1(AC[1]), .SHL(SHL), .AC_i_1_2(AC_i_1), .Ii(OUT[0]), .Ci(Cin),
    .C_i_1(n1_bit_als_unit_1_c_i_1));
  _1_bit_ALS_unit u_1_bit_als_unit_2 (
    .AC_i(AC[1]), .DR_i(DR[1]), .AND(AND), .ADD(ADD), .DR(DR_2), .INPR(INPR), .INPR_i(INPR_IN[1]), .COM(COM),
    .SHR(SHR), .AC_i_1(AC[2]), .SHL(SHL), .AC_i_1_2(AC[0]), .Ii(OUT[1]), .Ci(n1_bit_als_unit_1_c_i_1),
    .C_i_1(n1_bit_als_unit_2_c_i_1));
  _1_bit_ALS_unit u_1_bit_als_unit_3 (
    .AC_i(AC[2]), .DR_i(DR[2]), .AND(AND), .ADD(ADD), .DR(DR_2), .INPR(INPR), .INPR_i(INPR_IN[2]), .COM(COM),
    .SHR(SHR), .AC_i_1(AC[3]), .SHL(SHL), .AC_i_1_2(AC[1]), .Ii(OUT[2]), .Ci(n1_bit_als_unit_2_c_i_1),
    .C_i_1(n1_bit_als_unit_3_c_i_1));
  _1_bit_ALS_unit u_1_bit_als_unit_4 (
    .AC_i(AC[3]), .DR_i(DR[3]), .AND(AND), .ADD(ADD), .DR(DR_2), .INPR(INPR), .INPR_i(INPR_IN[3]), .COM(COM),
    .SHR(SHR), .AC_i_1(AC[4]), .SHL(SHL), .AC_i_1_2(AC[2]), .Ii(OUT[3]), .Ci(n1_bit_als_unit_3_c_i_1),
    .C_i_1(n1_bit_als_unit_4_c_i_1));
  _1_bit_ALS_unit u_1_bit_als_unit_5 (
    .AC_i(AC[4]), .DR_i(DR[4]), .AND(AND), .ADD(ADD), .DR(DR_2), .INPR(INPR), .INPR_i(INPR_IN[4]), .COM(COM),
    .SHR(SHR), .AC_i_1(AC[5]), .SHL(SHL), .AC_i_1_2(AC[3]), .Ii(OUT[4]), .Ci(n1_bit_als_unit_4_c_i_1),
    .C_i_1(n1_bit_als_unit_5_c_i_1));
  _1_bit_ALS_unit u_1_bit_als_unit_6 (
    .AC_i(AC[5]), .DR_i(DR[5]), .AND(AND), .ADD(ADD), .DR(DR_2), .INPR(INPR), .INPR_i(INPR_IN[5]), .COM(COM),
    .SHR(SHR), .AC_i_1(AC[6]), .SHL(SHL), .AC_i_1_2(AC[4]), .Ii(OUT[5]), .Ci(n1_bit_als_unit_5_c_i_1),
    .C_i_1(n1_bit_als_unit_6_c_i_1));
  _1_bit_ALS_unit u_1_bit_als_unit_7 (
    .AC_i(AC[6]), .DR_i(DR[6]), .AND(AND), .ADD(ADD), .DR(DR_2), .INPR(INPR), .INPR_i(INPR_IN[6]), .COM(COM),
    .SHR(SHR), .AC_i_1(AC[7]), .SHL(SHL), .AC_i_1_2(AC[5]), .Ii(OUT[6]), .Ci(n1_bit_als_unit_6_c_i_1),
    .C_i_1(n1_bit_als_unit_7_c_i_1));
  _1_bit_ALS_unit u_1_bit_als_unit_8 (
    .AC_i(AC[7]), .DR_i(DR[7]), .AND(AND), .ADD(ADD), .DR(DR_2), .INPR(INPR), .INPR_i(INPR_IN[7]), .COM(COM),
    .SHR(SHR), .AC_i_1(AC[8]), .SHL(SHL), .AC_i_1_2(AC[6]), .Ii(OUT[7]), .Ci(n1_bit_als_unit_7_c_i_1),
    .C_i_1(n1_bit_als_unit_8_c_i_1));
  _1_bit_ALS_unit u_1_bit_als_unit_9 (
    .AC_i(AC[8]), .DR_i(DR[8]), .AND(AND), .ADD(ADD), .DR(DR_2), .INPR(INPR), .INPR_i(1'b0), .COM(COM),
    .SHR(SHR), .AC_i_1(AC[9]), .SHL(SHL), .AC_i_1_2(AC[7]), .Ii(OUT[8]), .Ci(n1_bit_als_unit_8_c_i_1),
    .C_i_1(n1_bit_als_unit_9_c_i_1));
  _1_bit_ALS_unit u_1_bit_als_unit_10 (
    .AC_i(AC[9]), .DR_i(DR[9]), .AND(AND), .ADD(ADD), .DR(DR_2), .INPR(INPR), .INPR_i(1'b0), .COM(COM),
    .SHR(SHR), .AC_i_1(AC[10]), .SHL(SHL), .AC_i_1_2(AC[8]), .Ii(OUT[9]), .Ci(n1_bit_als_unit_9_c_i_1),
    .C_i_1(n1_bit_als_unit_10_c_i_1));
  _1_bit_ALS_unit u_1_bit_als_unit_11 (
    .AC_i(AC[10]), .DR_i(DR[10]), .AND(AND), .ADD(ADD), .DR(DR_2), .INPR(INPR), .INPR_i(1'b0), .COM(COM),
    .SHR(SHR), .AC_i_1(AC[11]), .SHL(SHL), .AC_i_1_2(AC[9]), .Ii(OUT[10]), .Ci(n1_bit_als_unit_10_c_i_1),
    .C_i_1(n1_bit_als_unit_11_c_i_1));
  _1_bit_ALS_unit u_1_bit_als_unit_12 (
    .AC_i(AC[11]), .DR_i(DR[11]), .AND(AND), .ADD(ADD), .DR(DR_2), .INPR(INPR), .INPR_i(1'b0), .COM(COM),
    .SHR(SHR), .AC_i_1(AC[12]), .SHL(SHL), .AC_i_1_2(AC[10]), .Ii(OUT[11]), .Ci(n1_bit_als_unit_11_c_i_1),
    .C_i_1(n1_bit_als_unit_12_c_i_1));
  _1_bit_ALS_unit u_1_bit_als_unit_13 (
    .AC_i(AC[12]), .DR_i(DR[12]), .AND(AND), .ADD(ADD), .DR(DR_2), .INPR(INPR), .INPR_i(1'b0), .COM(COM),
    .SHR(SHR), .AC_i_1(AC[13]), .SHL(SHL), .AC_i_1_2(AC[11]), .Ii(OUT[12]), .Ci(n1_bit_als_unit_12_c_i_1),
    .C_i_1(n1_bit_als_unit_13_c_i_1));
  _1_bit_ALS_unit u_1_bit_als_unit_14 (
    .AC_i(AC[13]), .DR_i(DR[13]), .AND(AND), .ADD(ADD), .DR(DR_2), .INPR(INPR), .INPR_i(1'b0), .COM(COM),
    .SHR(SHR), .AC_i_1(AC[14]), .SHL(SHL), .AC_i_1_2(AC[12]), .Ii(OUT[13]), .Ci(n1_bit_als_unit_13_c_i_1),
    .C_i_1(n1_bit_als_unit_14_c_i_1));
  _1_bit_ALS_unit u_1_bit_als_unit_15 (
    .AC_i(AC[14]), .DR_i(DR[14]), .AND(AND), .ADD(ADD), .DR(DR_2), .INPR(INPR), .INPR_i(1'b0), .COM(COM),
    .SHR(SHR), .AC_i_1(AC[15]), .SHL(SHL), .AC_i_1_2(AC[13]), .Ii(OUT[14]), .Ci(n1_bit_als_unit_14_c_i_1),
    .C_i_1(n1_bit_als_unit_15_c_i_1));
  _1_bit_ALS_unit u_1_bit_als_unit_16 (
    .AC_i(AC[15]), .DR_i(DR[15]), .AND(AND), .ADD(ADD), .DR(DR_2), .INPR(INPR), .INPR_i(1'b0), .COM(COM),
    .SHR(SHR), .AC_i_1(AC_i_1_2), .SHL(SHL), .AC_i_1_2(AC[14]), .Ii(OUT[15]), .Ci(n1_bit_als_unit_15_c_i_1),
    .C_i_1(Cout));
endmodule

module _1_bit_ALS_unit (
  input  AC_i,
  input  Ci,
  input  DR_i,
  input  AND,
  input  ADD,
  input  DR,
  input  INPR,
  input  INPR_i,
  input  COM,
  input  SHR,
  input  AC_i_1,
  input  SHL,
  input  AC_i_1_2,
  output Ii,
  output C_i_1
);

  wire adder_1_out, and_1_out, and_2_out, and_3_out, and_4_out, and_5_out, and_6_out, and_7_out, not_1_out;

  Adder #(.width(1)) adder_1 (.a(AC_i), .b(DR_i), .out(adder_1_out), .cin(Ci), .cout(C_i_1));
  not not_1 (not_1_out, AC_i);
  and and_1 (and_1_out, AND, AC_i, DR_i);
  and and_2 (and_2_out, ADD, adder_1_out);
  and and_3 (and_3_out, DR, DR_i);
  and and_4 (and_4_out, INPR, INPR_i);
  and and_5 (and_5_out, COM, not_1_out);
  and and_6 (and_6_out, SHR, AC_i_1);
  and and_7 (and_7_out, SHL, AC_i_1_2);
  or or_1 (Ii, and_1_out, and_2_out, and_3_out, and_4_out, and_5_out, and_6_out, and_7_out);
endmodule

module Combined_16_bit_Register (
  input  CLR,
  input  LOAD,
  input  INR,
  input  [15:0] IN,
  input  CLK,
  output [15:0] OUT,
  output STAGE
);

  _16_Bit_Register u_16_bit_register_1 (
    .CLR(CLR), .LOAD(LOAD), .INR(INR), .I0(IN[0]), .I1(IN[1]), .I2(IN[2]), .I3(IN[3]), .I4(IN[4]),
    .I5(IN[5]), .I6(IN[6]), .I7(IN[7]), .I8(IN[8]), .I9(IN[9]), .I10(IN[10]), .I11(IN[11]), .I12(IN[12]),
    .I13(IN[13]), .I14(IN[14]), .I15(IN[15]), .A0(OUT[0]), .A1(OUT[1]), .A2(OUT[2]), .A3(OUT[3]),
    .A4(OUT[4]), .A5(OUT[5]), .A6(OUT[6]), .A7(OUT[7]), .A8(OUT[8]), .A9(OUT[9]), .A10(OUT[10]),
    .A11(OUT[11]), .A12(OUT[12]), .A13(OUT[13]), .A14(OUT[14]), .A15(OUT[15]), .Stage_out(STAGE), .CLK(CLK));
endmodule

module Combined_12_bit_Register (
  input  CLR,
  input  LOAD,
  input  INR,
  input  [11:0] IN,
  input  CLR_AS,
  input  CLK,
  output [11:0] OUT,
  output STAGE
);

  _12_Bit_Register u_12_bit_register_1 (
    .CLR(CLR), .LOAD(LOAD), .INR(INR), .I0(IN[0]), .I1(IN[1]), .I2(IN[2]), .I3(IN[3]), .I4(IN[4]),
    .I5(IN[5]), .I6(IN[6]), .I7(IN[7]), .I8(IN[8]), .I9(IN[9]), .I10(IN[10]), .I11(IN[11]), .CLK(CLK),
    .A0(OUT[0]), .A1(OUT[1]), .A2(OUT[2]), .A3(OUT[3]), .A4(OUT[4]), .A5(OUT[5]), .A6(OUT[6]), .A7(OUT[7]),
    .A8(OUT[8]), .A9(OUT[9]), .A10(OUT[10]), .A11(OUT[11]), .STAGE(STAGE), .CLR_AS(CLR_AS));
endmodule

module _16_Bit_Register (
  input  CLR,
  input  LOAD,
  input  INR,
  input  I0,
  input  I1,
  input  I2,
  input  I3,
  input  I4,
  input  I5,
  input  I6,
  input  I7,
  input  I8,
  input  I9,
  input  I10,
  input  I11,
  input  I12,
  input  I13,
  input  I14,
  input  I15,
  input  CLK,
  output A0,
  output A1,
  output A2,
  output A3,
  output A4,
  output A5,
  output A6,
  output A7,
  output A8,
  output A9,
  output A10,
  output A11,
  output A12,
  output A13,
  output A14,
  output A15,
  output Stage_out
);

  wire and_1_out, and_2_out, and_3_out, and_4_out, and_5_out, and_6_out, and_7_out, and_8_out, and_9_out,
       and_10_out, and_11_out, and_12_out, and_13_out, and_14_out, and_15_out, and_16_out, and_17_out,
       and_18_out, and_19_out, and_20_out, and_21_out, and_22_out, and_23_out, and_24_out, and_25_out,
       and_26_out, and_27_out, and_28_out, and_29_out, and_30_out, and_31_out, and_32_out, and_33_out,
       and_34_out, and_35_out, and_36_out, and_37_out, and_38_out, and_39_out, and_40_out, and_41_out,
       and_42_out, and_43_out, and_44_out, and_45_out, and_46_out, and_47_out, and_48_out, and_49_out,
       not_1_out, not_2_out, not_3_out, not_4_out, not_5_out, not_6_out, not_7_out, not_8_out, not_9_out,
       not_10_out, not_11_out, not_12_out, not_13_out, not_14_out, not_15_out, not_16_out, not_17_out,
       not_18_out, or_1_out, or_2_out, or_3_out, or_4_out, or_5_out, or_6_out, or_7_out, or_8_out, or_9_out,
       or_10_out, or_11_out, or_12_out, or_13_out, or_14_out, or_15_out, or_16_out, or_17_out, or_18_out,
       or_19_out, or_20_out, or_21_out, or_22_out, or_23_out, or_24_out, or_25_out, or_26_out, or_27_out,
       or_28_out, or_29_out, or_30_out, or_31_out, or_32_out;

  not not_1 (not_1_out, CLR);
  not not_2 (not_2_out, LOAD);
  and and_1 (and_1_out, not_1_out, LOAD);
  not not_3 (not_3_out, I0);
  not not_4 (not_4_out, I1);
  not not_5 (not_5_out, I2);
  not not_6 (not_6_out, I3);
  not not_7 (not_7_out, I4);
  not not_8 (not_8_out, I5);
  not not_9 (not_9_out, I6);
  not not_10 (not_10_out, I7);
  not not_11 (not_11_out, I8);
  not not_12 (not_12_out, I9);
  not not_13 (not_13_out, I10);
  not not_14 (not_14_out, I11);
  not not_15 (not_15_out, I12);
  not not_16 (not_16_out, I13);
  not not_17 (not_17_out, I14);
  not not_18 (not_18_out, I15);
  and and_2 (and_2_out, not_1_out, not_2_out, INR);
  and and_3 (and_3_out, and_1_out, I0);
  and and_4 (and_4_out, and_1_out, not_3_out);
  and and_5 (and_5_out, and_2_out, A0);
  and and_6 (and_6_out, and_1_out, I1);
  and and_7 (and_7_out, and_1_out, not_4_out);
  and and_8 (and_8_out, and_5_out, A1);
  and and_9 (and_9_out, and_1_out, I2);
  and and_10 (and_10_out, and_1_out, not_5_out);
  and and_11 (and_11_out, and_8_out, A2);
  and and_12 (and_12_out, and_1_out, I3);
  and and_13 (and_13_out, and_1_out, not_6_out);
  and and_14 (and_14_out, and_11_out, A3);
  and and_15 (and_15_out, and_1_out, I4);
  and and_16 (and_16_out, and_1_out, not_7_out);
  and and_17 (and_17_out, and_14_out, A4);
  and and_18 (and_18_out, and_1_out, I5);
  and and_19 (and_19_out, and_1_out, not_8_out);
  and and_20 (and_20_out, and_17_out, A5);
  and and_21 (and_21_out, and_1_out, I6);
  and and_22 (and_22_out, and_1_out, not_9_out);
  and and_23 (and_23_out, and_20_out, A6);
  and and_24 (and_24_out, and_1_out, I7);
  and and_25 (and_25_out, and_1_out, not_10_out);
  and and_26 (and_26_out, and_23_out, A7);
  and and_27 (and_27_out, and_1_out, I8);
  and and_28 (and_28_out, and_1_out, not_11_out);
  and and_29 (and_29_out, and_26_out, A8);
  and and_30 (and_30_out, and_1_out, I9);
  and and_31 (and_31_out, and_1_out, not_12_out);
  and and_32 (and_32_out, and_29_out, A9);
  and and_33 (and_33_out, and_1_out, I10);
  and and_34 (and_34_out, and_1_out, not_13_out);
  and and_35 (and_35_out, and_32_out, A10);
  and and_36 (and_36_out, and_1_out, I11);
  and and_37 (and_37_out, and_1_out, not_14_out);
  and and_38 (and_38_out, and_35_out, A11);
  and and_39 (and_39_out, and_1_out, I12);
  and and_40 (and_40_out, and_1_out, not_15_out);
  and and_41 (and_41_out, and_38_out, A12);
  and and_42 (and_42_out, and_1_out, I13);
  and and_43 (and_43_out, and_1_out, not_16_out);
  and and_44 (and_44_out, and_41_out, A13);
  and and_45 (and_45_out, and_1_out, I14);
  and and_46 (and_46_out, and_1_out, not_17_out);
  and and_47 (and_47_out, and_44_out, A14);
  and and_48 (and_48_out, and_1_out, I15);
  and and_49 (and_49_out, and_1_out, not_18_out);
  and and_50 (Stage_out, and_47_out, A15);
  or or_1 (or_1_out, and_2_out, and_3_out);
  or or_2 (or_2_out, CLR, and_2_out, and_4_out);
  or or_3 (or_3_out, and_5_out, and_6_out);
  or or_4 (or_4_out, CLR, and_5_out, and_7_out);
  or or_5 (or_5_out, and_8_out, and_9_out);
  or or_6 (or_6_out, CLR, and_8_out, and_10_out);
  or or_7 (or_7_out, and_11_out, and_12_out);
  or or_8 (or_8_out, CLR, and_11_out, and_13_out);
  or or_9 (or_9_out, and_14_out, and_15_out);
  or or_10 (or_10_out, CLR, and_14_out, and_16_out);
  or or_11 (or_11_out, and_17_out, and_18_out);
  or or_12 (or_12_out, CLR, and_17_out, and_19_out);
  or or_13 (or_13_out, and_20_out, and_21_out);
  or or_14 (or_14_out, CLR, and_20_out, and_22_out);
  or or_15 (or_15_out, and_23_out, and_24_out);
  or or_16 (or_16_out, CLR, and_23_out, and_25_out);
  or or_17 (or_17_out, and_26_out, and_27_out);
  or or_18 (or_18_out, CLR, and_26_out, and_28_out);
  or or_19 (or_19_out, and_29_out, and_30_out);
  or or_20 (or_20_out, CLR, and_29_out, and_31_out);
  or or_21 (or_21_out, and_32_out, and_33_out);
  or or_22 (or_22_out, CLR, and_32_out, and_34_out);
  or or_23 (or_23_out, and_35_out, and_36_out);
  or or_24 (or_24_out, CLR, and_35_out, and_37_out);
  or or_25 (or_25_out, and_38_out, and_39_out);
  or or_26 (or_26_out, CLR, and_38_out, and_40_out);
  or or_27 (or_27_out, and_41_out, and_42_out);
  or or_28 (or_28_out, CLR, and_41_out, and_43_out);
  or or_29 (or_29_out, and_44_out, and_45_out);
  or or_30 (or_30_out, CLR, and_44_out, and_46_out);
  or or_31 (or_31_out, and_47_out, and_48_out);
  or or_32 (or_32_out, CLR, and_47_out, and_49_out);
  J_K_Flip_Flop j_k_ff_1 (.J(or_1_out), .clk(CLK), .K(or_2_out), .Q(A0));  // open: Qn, preset, en, reset
  J_K_Flip_Flop j_k_ff_2 (.J(or_3_out), .clk(CLK), .K(or_4_out), .Q(A1));  // open: Qn, preset, en, reset
  J_K_Flip_Flop j_k_ff_3 (.J(or_5_out), .clk(CLK), .K(or_6_out), .Q(A2));  // open: Qn, preset, en, reset
  J_K_Flip_Flop j_k_ff_4 (.J(or_7_out), .clk(CLK), .K(or_8_out), .Q(A3));  // open: Qn, preset, en, reset
  J_K_Flip_Flop j_k_ff_5 (.J(or_9_out), .clk(CLK), .K(or_10_out), .Q(A4));  // open: Qn, preset, en, reset
  J_K_Flip_Flop j_k_ff_6 (.J(or_11_out), .clk(CLK), .K(or_12_out), .Q(A5));  // open: Qn, preset, en, reset
  J_K_Flip_Flop j_k_ff_7 (.J(or_13_out), .clk(CLK), .K(or_14_out), .Q(A6));  // open: Qn, preset, en, reset
  J_K_Flip_Flop j_k_ff_8 (.J(or_15_out), .clk(CLK), .K(or_16_out), .Q(A7));  // open: Qn, preset, en, reset
  J_K_Flip_Flop j_k_ff_9 (.J(or_17_out), .clk(CLK), .K(or_18_out), .Q(A8));  // open: Qn, preset, en, reset
  J_K_Flip_Flop j_k_ff_10 (.J(or_19_out), .clk(CLK), .K(or_20_out), .Q(A9));  // open: Qn, preset, en, reset
  J_K_Flip_Flop j_k_ff_11 (.J(or_21_out), .clk(CLK), .K(or_22_out), .Q(A10));  // open: Qn, preset, en, reset
  J_K_Flip_Flop j_k_ff_12 (.J(or_23_out), .clk(CLK), .K(or_24_out), .Q(A11));  // open: Qn, preset, en, reset
  J_K_Flip_Flop j_k_ff_13 (.J(or_25_out), .clk(CLK), .K(or_26_out), .Q(A12));  // open: Qn, preset, en, reset
  J_K_Flip_Flop j_k_ff_14 (.J(or_27_out), .clk(CLK), .K(or_28_out), .Q(A13));  // open: Qn, preset, en, reset
  J_K_Flip_Flop j_k_ff_15 (.J(or_29_out), .clk(CLK), .K(or_30_out), .Q(A14));  // open: Qn, preset, en, reset
  J_K_Flip_Flop j_k_ff_16 (.J(or_31_out), .clk(CLK), .K(or_32_out), .Q(A15));  // open: Qn, preset, en, reset
endmodule

module _12_Bit_Register (
  input  CLR,
  input  LOAD,
  input  INR,
  input  I0,
  input  I1,
  input  I2,
  input  I3,
  input  I4,
  input  I5,
  input  I6,
  input  I7,
  input  I8,
  input  I9,
  input  I10,
  input  I11,
  input  CLR_AS,
  input  CLK,
  output A0,
  output A1,
  output A2,
  output A3,
  output A4,
  output A5,
  output A6,
  output A7,
  output A8,
  output A9,
  output A10,
  output A11,
  output STAGE
);

  wire and_1_out, and_2_out, and_3_out, and_4_out, and_5_out, and_6_out, and_7_out, and_8_out, and_9_out,
       and_10_out, and_11_out, and_12_out, and_13_out, and_14_out, and_15_out, and_16_out, and_17_out,
       and_18_out, and_19_out, and_20_out, and_21_out, and_22_out, and_23_out, and_24_out, and_25_out,
       and_26_out, and_27_out, and_28_out, and_29_out, and_30_out, and_31_out, and_32_out, and_33_out,
       and_34_out, and_35_out, and_36_out, and_37_out, not_1_out, not_2_out, not_3_out, not_4_out, not_5_out,
       not_6_out, not_7_out, not_8_out, not_9_out, not_10_out, not_11_out, not_12_out, not_13_out,
       not_14_out, or_1_out, or_2_out, or_3_out, or_4_out, or_5_out, or_6_out, or_7_out, or_8_out, or_9_out,
       or_10_out, or_11_out, or_12_out, or_13_out, or_14_out, or_15_out, or_16_out, or_17_out, or_18_out,
       or_19_out, or_20_out, or_21_out, or_22_out, or_23_out, or_24_out;

  not not_1 (not_1_out, CLR);
  and and_1 (and_1_out, not_1_out, LOAD);
  not not_2 (not_2_out, LOAD);
  not not_3 (not_3_out, I0);
  not not_4 (not_4_out, I1);
  not not_5 (not_5_out, I2);
  not not_6 (not_6_out, I3);
  not not_7 (not_7_out, I4);
  not not_8 (not_8_out, I5);
  not not_9 (not_9_out, I6);
  not not_10 (not_10_out, I7);
  not not_11 (not_11_out, I8);
  not not_12 (not_12_out, I9);
  not not_13 (not_13_out, I10);
  not not_14 (not_14_out, I11);
  and and_2 (and_2_out, not_1_out, not_2_out, INR);
  and and_3 (and_3_out, and_1_out, I0);
  and and_4 (and_4_out, and_1_out, not_3_out);
  and and_5 (and_5_out, and_1_out, I1);
  and and_6 (and_6_out, and_1_out, not_4_out);
  and and_7 (and_7_out, and_1_out, I2);
  and and_8 (and_8_out, and_1_out, not_5_out);
  and and_9 (and_9_out, and_1_out, I3);
  and and_10 (and_10_out, and_1_out, not_6_out);
  and and_11 (and_11_out, and_1_out, I4);
  and and_12 (and_12_out, and_1_out, not_7_out);
  and and_13 (and_13_out, and_1_out, I5);
  and and_14 (and_14_out, and_1_out, not_8_out);
  and and_15 (and_15_out, and_1_out, I6);
  and and_16 (and_16_out, and_1_out, not_9_out);
  and and_17 (and_17_out, and_1_out, I7);
  and and_18 (and_18_out, and_1_out, not_10_out);
  and and_19 (and_19_out, and_1_out, I8);
  and and_20 (and_20_out, and_1_out, not_11_out);
  and and_21 (and_21_out, and_1_out, I9);
  and and_22 (and_22_out, and_1_out, not_12_out);
  and and_23 (and_23_out, and_1_out, I10);
  and and_24 (and_24_out, and_1_out, not_13_out);
  and and_25 (and_25_out, and_1_out, I11);
  and and_26 (and_26_out, and_1_out, not_14_out);
  and and_27 (and_27_out, and_2_out, A0);
  and and_28 (and_28_out, and_27_out, A1);
  and and_29 (and_29_out, and_28_out, A2);
  and and_30 (and_30_out, and_29_out, A3);
  and and_31 (and_31_out, and_30_out, A4);
  and and_32 (and_32_out, and_31_out, A5);
  and and_33 (and_33_out, and_32_out, A6);
  and and_34 (and_34_out, and_33_out, A7);
  and and_35 (and_35_out, and_34_out, A8);
  and and_36 (and_36_out, and_35_out, A9);
  and and_37 (and_37_out, and_36_out, A10);
  and and_38 (STAGE, and_37_out, A11);
  or or_1 (or_1_out, and_2_out, and_3_out);
  or or_2 (or_2_out, CLR, and_2_out, and_4_out);
  or or_3 (or_3_out, and_27_out, and_5_out);
  or or_4 (or_4_out, CLR, and_27_out, and_6_out);
  or or_5 (or_5_out, and_28_out, and_7_out);
  or or_6 (or_6_out, CLR, and_28_out, and_8_out);
  or or_7 (or_7_out, and_29_out, and_9_out);
  or or_8 (or_8_out, CLR, and_29_out, and_10_out);
  or or_9 (or_9_out, and_30_out, and_11_out);
  or or_10 (or_10_out, CLR, and_30_out, and_12_out);
  or or_11 (or_11_out, and_31_out, and_13_out);
  or or_12 (or_12_out, CLR, and_31_out, and_14_out);
  or or_13 (or_13_out, and_32_out, and_15_out);
  or or_14 (or_14_out, CLR, and_32_out, and_16_out);
  or or_15 (or_15_out, and_33_out, and_17_out);
  or or_16 (or_16_out, CLR, and_33_out, and_18_out);
  or or_17 (or_17_out, and_34_out, and_19_out);
  or or_18 (or_18_out, CLR, and_34_out, and_20_out);
  or or_19 (or_19_out, and_35_out, and_21_out);
  or or_20 (or_20_out, CLR, and_35_out, and_22_out);
  or or_21 (or_21_out, and_36_out, and_23_out);
  or or_22 (or_22_out, CLR, and_36_out, and_24_out);
  or or_23 (or_23_out, and_37_out, and_25_out);
  or or_24 (or_24_out, CLR, and_37_out, and_26_out);
  J_K_Flip_Flop j_k_ff_1 (.J(or_1_out), .clk(CLK), .K(or_2_out), .Q(A0), .reset(CLR_AS));  // open: Qn, preset, en
  J_K_Flip_Flop j_k_ff_2 (.J(or_3_out), .clk(CLK), .K(or_4_out), .Q(A1), .reset(CLR_AS));  // open: Qn, preset, en
  J_K_Flip_Flop j_k_ff_3 (.J(or_5_out), .clk(CLK), .K(or_6_out), .Q(A2), .reset(CLR_AS));  // open: Qn, preset, en
  J_K_Flip_Flop j_k_ff_4 (.J(or_7_out), .clk(CLK), .K(or_8_out), .Q(A3), .reset(CLR_AS));  // open: Qn, preset, en
  J_K_Flip_Flop j_k_ff_5 (.J(or_9_out), .clk(CLK), .K(or_10_out), .Q(A4), .reset(CLR_AS));  // open: Qn, preset, en
  J_K_Flip_Flop j_k_ff_6 (.J(or_11_out), .clk(CLK), .K(or_12_out), .Q(A5), .reset(CLR_AS));  // open: Qn, preset, en
  J_K_Flip_Flop j_k_ff_7 (.J(or_13_out), .clk(CLK), .K(or_14_out), .Q(A6), .reset(CLR_AS));  // open: Qn, preset, en
  J_K_Flip_Flop j_k_ff_8 (.J(or_15_out), .clk(CLK), .K(or_16_out), .Q(A7), .reset(CLR_AS));  // open: Qn, preset, en
  J_K_Flip_Flop j_k_ff_9 (.J(or_17_out), .clk(CLK), .K(or_18_out), .Q(A8), .reset(CLR_AS));  // open: Qn, preset, en
  J_K_Flip_Flop j_k_ff_10 (.J(or_19_out), .clk(CLK), .K(or_20_out), .Q(A9), .reset(CLR_AS));  // open: Qn, preset, en
  J_K_Flip_Flop j_k_ff_11 (.J(or_21_out), .clk(CLK), .K(or_22_out), .Q(A10), .reset(CLR_AS));  // open: Qn, preset, en
  J_K_Flip_Flop j_k_ff_12 (.J(or_23_out), .clk(CLK), .K(or_24_out), .Q(A11), .reset(CLR_AS));  // open: Qn, preset, en
endmodule

module _8_Bit_Register (
  input  CLR,
  input  LOAD,
  input  INR,
  input  [7:0] IN,
  input  CLK,
  output [7:0] OUT,
  output STAGE
);

  wire and_1_out, and_2_out, and_3_out, and_4_out, and_5_out, and_6_out, and_7_out, and_8_out, and_9_out,
       and_10_out, and_11_out, and_12_out, and_13_out, and_14_out, and_15_out, and_16_out, and_17_out,
       and_18_out, and_19_out, and_20_out, and_21_out, and_22_out, and_23_out, and_24_out, and_25_out,
       not_1_out, not_2_out, not_3_out, not_4_out, not_5_out, not_6_out, not_7_out, not_8_out, not_9_out,
       not_10_out, or_1_out, or_2_out, or_3_out, or_4_out, or_5_out, or_6_out, or_7_out, or_8_out, or_9_out,
       or_10_out, or_11_out, or_12_out, or_13_out, or_14_out, or_15_out, or_16_out;

  not not_1 (not_1_out, CLR);
  and and_1 (and_1_out, not_1_out, LOAD);
  not not_2 (not_2_out, LOAD);
  not not_3 (not_3_out, IN[0]);
  not not_4 (not_4_out, IN[1]);
  not not_5 (not_5_out, IN[2]);
  not not_6 (not_6_out, IN[3]);
  not not_7 (not_7_out, IN[4]);
  not not_8 (not_8_out, IN[5]);
  not not_9 (not_9_out, IN[6]);
  not not_10 (not_10_out, IN[7]);
  and and_2 (and_2_out, not_1_out, not_2_out, INR);
  and and_3 (and_3_out, and_1_out, IN[0]);
  and and_4 (and_4_out, and_1_out, not_3_out);
  and and_5 (and_5_out, and_1_out, IN[1]);
  and and_6 (and_6_out, and_1_out, not_4_out);
  and and_7 (and_7_out, and_1_out, IN[2]);
  and and_8 (and_8_out, and_1_out, not_5_out);
  and and_9 (and_9_out, and_1_out, IN[3]);
  and and_10 (and_10_out, and_1_out, not_6_out);
  and and_11 (and_11_out, and_1_out, IN[4]);
  and and_12 (and_12_out, and_1_out, not_7_out);
  and and_13 (and_13_out, and_1_out, IN[5]);
  and and_14 (and_14_out, and_1_out, not_8_out);
  and and_15 (and_15_out, and_1_out, IN[6]);
  and and_16 (and_16_out, and_1_out, not_9_out);
  and and_17 (and_17_out, and_1_out, IN[7]);
  and and_18 (and_18_out, and_1_out, not_10_out);
  and and_19 (and_19_out, and_2_out, OUT[0]);
  and and_20 (and_20_out, and_19_out, OUT[1]);
  and and_21 (and_21_out, and_20_out, OUT[2]);
  and and_22 (and_22_out, and_21_out, OUT[3]);
  and and_23 (and_23_out, and_22_out, OUT[4]);
  and and_24 (and_24_out, and_23_out, OUT[5]);
  and and_25 (and_25_out, and_24_out, OUT[6]);
  and and_26 (STAGE, and_25_out, OUT[7]);
  or or_1 (or_1_out, and_2_out, and_3_out);
  or or_2 (or_2_out, CLR, and_2_out, and_4_out);
  or or_3 (or_3_out, and_19_out, and_5_out);
  or or_4 (or_4_out, CLR, and_19_out, and_6_out);
  or or_5 (or_5_out, and_20_out, and_7_out);
  or or_6 (or_6_out, CLR, and_20_out, and_8_out);
  or or_7 (or_7_out, and_21_out, and_9_out);
  or or_8 (or_8_out, CLR, and_21_out, and_10_out);
  or or_9 (or_9_out, and_22_out, and_11_out);
  or or_10 (or_10_out, CLR, and_22_out, and_12_out);
  or or_11 (or_11_out, and_23_out, and_13_out);
  or or_12 (or_12_out, CLR, and_23_out, and_14_out);
  or or_13 (or_13_out, and_24_out, and_15_out);
  or or_14 (or_14_out, CLR, and_24_out, and_16_out);
  or or_15 (or_15_out, and_25_out, and_17_out);
  or or_16 (or_16_out, CLR, and_25_out, and_18_out);
  J_K_Flip_Flop j_k_ff_1 (.J(or_1_out), .clk(CLK), .K(or_2_out), .Q(OUT[0]));  // open: Qn, preset, en, reset
  J_K_Flip_Flop j_k_ff_2 (.J(or_3_out), .clk(CLK), .K(or_4_out), .Q(OUT[1]));  // open: Qn, preset, en, reset
  J_K_Flip_Flop j_k_ff_3 (.J(or_5_out), .clk(CLK), .K(or_6_out), .Q(OUT[2]));  // open: Qn, preset, en, reset
  J_K_Flip_Flop j_k_ff_4 (.J(or_7_out), .clk(CLK), .K(or_8_out), .Q(OUT[3]));  // open: Qn, preset, en, reset
  J_K_Flip_Flop j_k_ff_5 (.J(or_9_out), .clk(CLK), .K(or_10_out), .Q(OUT[4]));  // open: Qn, preset, en, reset
  J_K_Flip_Flop j_k_ff_6 (.J(or_11_out), .clk(CLK), .K(or_12_out), .Q(OUT[5]));  // open: Qn, preset, en, reset
  J_K_Flip_Flop j_k_ff_7 (.J(or_13_out), .clk(CLK), .K(or_14_out), .Q(OUT[6]));  // open: Qn, preset, en, reset
  J_K_Flip_Flop j_k_ff_8 (.J(or_15_out), .clk(CLK), .K(or_16_out), .Q(OUT[7]));  // open: Qn, preset, en, reset
endmodule

// SC
module _4_Bit_Rgister (
  input  CLR,
  input  LOAD,
  input  INR,
  input  I0,
  input  I1,
  input  I2,
  input  I3,
  input  CLK,
  output A0,
  output A1,
  output A2,
  output A3,
  output STAGE
);

  wire and_1_out, and_2_out, and_3_out, and_4_out, and_5_out, and_6_out, and_7_out, and_8_out, and_9_out,
       and_10_out, and_11_out, and_12_out, and_13_out, not_1_out, not_2_out, not_3_out, not_4_out, not_5_out,
       not_6_out, or_1_out, or_2_out, or_3_out, or_4_out, or_5_out, or_6_out, or_7_out, or_8_out;

  not not_1 (not_1_out, CLR);
  not not_2 (not_2_out, LOAD);
  and and_1 (and_1_out, not_1_out, LOAD);
  not not_3 (not_3_out, I0);
  not not_4 (not_4_out, I1);
  not not_5 (not_5_out, I2);
  not not_6 (not_6_out, I3);
  and and_2 (and_2_out, not_1_out, not_2_out, INR);
  and and_3 (and_3_out, and_1_out, I0);
  and and_4 (and_4_out, and_1_out, not_3_out);
  and and_5 (and_5_out, and_2_out, A0);
  and and_6 (and_6_out, and_1_out, I1);
  and and_7 (and_7_out, and_1_out, not_4_out);
  and and_8 (and_8_out, and_5_out, A1);
  and and_9 (and_9_out, and_1_out, I2);
  and and_10 (and_10_out, and_1_out, not_5_out);
  and and_11 (and_11_out, and_8_out, A2);
  and and_12 (and_12_out, and_1_out, I3);
  and and_13 (and_13_out, and_1_out, not_6_out);
  and and_14 (STAGE, and_11_out, A3);
  or or_1 (or_1_out, and_2_out, and_3_out);
  or or_2 (or_2_out, CLR, and_2_out, and_4_out);
  or or_3 (or_3_out, and_5_out, and_6_out);
  or or_4 (or_4_out, CLR, and_5_out, and_7_out);
  or or_5 (or_5_out, and_8_out, and_9_out);
  or or_6 (or_6_out, CLR, and_8_out, and_10_out);
  or or_7 (or_7_out, and_11_out, and_12_out);
  or or_8 (or_8_out, CLR, and_11_out, and_13_out);
  J_K_Flip_Flop j_k_ff_1 (.J(or_1_out), .clk(CLK), .K(or_2_out), .Q(A0));  // open: Qn, preset, en, reset
  J_K_Flip_Flop j_k_ff_2 (.J(or_3_out), .clk(CLK), .K(or_4_out), .Q(A1));  // open: Qn, preset, en, reset
  J_K_Flip_Flop j_k_ff_3 (.J(or_5_out), .clk(CLK), .K(or_6_out), .Q(A2));  // open: Qn, preset, en, reset
  J_K_Flip_Flop j_k_ff_4 (.J(or_7_out), .clk(CLK), .K(or_8_out), .Q(A3));  // open: Qn, preset, en, reset
endmodule

module Encoder (
  input  x1,
  input  x2,
  input  x3,
  input  x4,
  input  x5,
  input  x6,
  input  x7,
  output [2:0] out
);

  or or_1 (out[0], x1, x3, x5, x7);
  or or_2 (out[1], x2, x3, x6, x7);
  or or_3 (out[2], x4, x5, x6, x7);
endmodule
